# Fritzing sketch BarzinFarahani_lab4diagram (saved by Fritzing 0.9.6b)
breadboards: 1

parts:
  Resistor_(Green) = Resistor [tolerance=±5% resistance=220 package="2512 [SMD]"]
  Resistor_(Blue) = Resistor [tolerance=±5% resistance=220 package="2512 [SMD]"]
  Resistor_(Red) = Resistor [tolerance=±5% resistance=220 package="2512 [SMD]"]
  Teensy_3_2 = Teensy 3.2  # not connected
  S1 = Momentary Switch [package=ksa_sealed_tac_switch]
  S2 = Pushbutton [package="[SMD]"]
  LED1 = RGB LED - (4 legs) [package="5 mm [THT]"]
  R1 = Resistor [tolerance=±5% power=0.25 resistance=220 package=THT]

nets:
  N1: Resistor_(Green).Pin_0, LED1.blue_cathode
  N2: Resistor_(Blue).Pin_0, LED1.common_anode
  N3: Resistor_(Red).Pin_0, LED1.red_cathode
  N4: S1.2, S2.Pin_1, S2.Pin_2, LED1.green_cathode
  N5: S1.3, R1.Pin_1
  N6: S2.Pin_3, S2.Pin_4

notes:
  CST8227 – Interfacing
  Lab 04 – Pushbuttons to Control LED Colors Control a tri-color RGB with two switches and a pull-up resistor.
  @Barzin Farahani (40922695)

custom parts:
  Teensy 3.2: The Teensy is a complete USB-based microcontoller development system, in a very small footprint, capable of implementing many types of projects. All programming is done via the USB port. No special programmer is needed, only a standard micro-USB cable and a PC or Macintosh with a USB port. It has a USB keyboard/mouse/joystick emulation stack and can be programmed through Arduino IDE.
