# Fritzing sketch Lab6_BarzinFarahani (saved by Fritzing 0.9.6b)
breadboards: 1

parts:
  LED1 = RGB LED (com. cathode, rgb) [package="5 mm [THT]"]
  Resistor_(Green_LED) = Resistor [tolerance=±5% resistance=220 package="2512 [SMD]"]
  Resistor_(Blue_LED) = Resistor [tolerance=±5% resistance=220 package="2512 [SMD]"]
  Resistor_(Red_LED) = Resistor [tolerance=±5% resistance=220 package="2512 [SMD]"]
  Potentiometer = Trimmer Potentiometer [maximum_resistance=25kΩ package=THT]
  Teensy_3_2 = Teensy 3.2  # not connected

nets:
  N1: LED1.red_anode, Resistor_(Red_LED).Pin_0
  N2: LED1.common_cathode, Resistor_(Blue_LED).Pin_0
  N3: LED1.green_anode, Potentiometer.leg1
  N4: LED1.blue_anode, Resistor_(Green_LED).Pin_0

notes:
  CST8227 – Interfacing
  Lab 06 – User Controlled LED Color
  Use a potentiometer as user input to control the LED color.
  @author Barzin Farahani (40922695)

custom parts:
  Teensy 3.2: The Teensy is a complete USB-based microcontoller development system, in a very small footprint, capable of implementing many types of projects. All programming is done via the USB port. No special programmer is needed, only a standard micro-USB cable and a PC or Macintosh with a USB port. It has a USB keyboard/mouse/joystick emulation stack and can be programmed through Arduino IDE.
